# Fritzing sketch pcdDesign (saved by Fritzing 0.9.3b)
circuit board: 5.54cm x 7.1cm
breadboards: 1

parts:
  GY1 = MPU-6050 Board GY-521 [form="♀ (female)" package=THT]
  R3 = Resistor [tolerance=±5% resistance=1k package=THT]
  R4 = Resistor [tolerance=±5% resistance=1k package=THT]
  R5 = Resistor [tolerance=±5% resistance=1k package=THT]
  U1 = NodeMCU V1.0
  R2 = Resistor [tolerance=±5% resistance=390k package=THT]
  R1 = Resistor [tolerance=±5% resistance=110k package=THT]
  LED1 = RGB LED (com. cathode, rgb) [package="5 mm [THT]"]

nets:
  N1: GY1.pin1, U1.Vin, R1.Pin_1
  N2: GY1.pin2, U1.GND, R2.Pin_0, LED1.common_cathode
  N3: GY1.pin3, U1.D1
  N4: GY1.pin4, U1.D2
  N5: R3.Pin_0, LED1.red_anode
  N6: R3.Pin_1, U1.D5
  N7: R4.Pin_0, LED1.green_anode
  N8: R4.Pin_1, U1.D6
  N9: R5.Pin_0, LED1.blue_anode
  N10: R5.Pin_1, U1.D7
  N11: U1.A0, R2.Pin_1, R1.Pin_0

custom parts:
  MPU-6050 Board GY-521: Acelerometro y Giroscopio MPU-6050 Board GY-521
  NodeMCU V1.0: ESP8266 based NodeMCU
